# Fritzing sketch eos_ttl_quench (saved by Fritzing 0.9.1b)
breadboards: 1

parts:
  R1 = Rotary Potentiometer (Small) [maximum_resistance=100kΩ package=THT]
  S1 = Pushbutton [package="[THT]"]
  C1 = Ceramic Capacitor [capacitance=100nF package="100 mil [THT, multilayer]"]
  Componente1 = Arduino Uno (Rev3)
  U1 = mystery part, 3 pins [chip_label="EOS TTL Hotshoe"]

nets:
  5V: R1.leg1, Componente1.5V
  N1: R1.wiper, Componente1.A0
  GND: R1.leg2, S1.Pin_3, S1.Pin_4, C1.0, Componente1.GND, U1.pin3
  N2: S1.Pin_1, S1.Pin_2, C1.1, Componente1.D2
  N3: Componente1.D8, U1.pin2
  N4: Componente1.D9_PWM, U1.pin1

notes:
  Center pin
  Quench pin
  Ground pin
  Canon TTL Hotshoe
  LPF/Debounce
  Trigger switch
  Delay time selector
